# Fritzing sketch DBC (saved by Fritzing 0.9.3b)
circuit board: 8.46667cm x 5.64444cm
breadboards: 1

parts:
  U2 = 7-SEGMENT-DISPLAY [package=7-segment-display]
  R2 = Resistor [tolerance=±5% resistance=220 package="1206 [SMD]"]
  R3 = Resistor [tolerance=±5% resistance=220 package="1206 [SMD]"]
  R4 = Resistor [tolerance=±5% resistance=220 package="1206 [SMD]"]
  R6 = Resistor [tolerance=±5% resistance=220 package="1206 [SMD]"]
  R7 = Resistor [tolerance=±5% resistance=220 package="1206 [SMD]"]
  R8 = Resistor [tolerance=±5% resistance=220 package="1206 [SMD]"]
  U1 = HEF4543 [part_number=\ package=dil16]
  R1 = Resistor [tolerance=±5% resistance=220 package="1206 [SMD]"]
  Onderdeel1 = Arduino Uno (Rev3)
  S1 = Pushbutton [package="[SMD]"]

nets:
  N1: U2.E, R3.Pin_1
  N2: U2.D, R6.Pin_1
  N3: U2.G1, R7.Pin_1
  GND: U2.C, U1.GND, Onderdeel1.GND, S1.Pin_1, S1.Pin_2
  N4: U2.DP, R8.Pin_0
  N5: U2.A, R1.Pin_0
  N6: U2.G2, R2.Pin_0
  N7: U2.G, R4.Pin_1
  N8: R2.Pin_1, U1.C
  N9: R3.Pin_0, U1.E
  N10: R4.Pin_0, U1.D
  N11: R6.Pin_0, U1.A
  N12: R7.Pin_0, U1.F
  N13: R8.Pin_1, U1.G
  N14: U1.LD, Onderdeel1.D10_PWM/SS
  N15: U1.D2, Onderdeel1.D12/MISO
  N16: U1.D1, S1.Pin_4
  N17: U1.PH, Onderdeel1.D11_PWM/MOSI
  N18: U1.BL, Onderdeel1.D13/SCK
  N19: U1.B, R1.Pin_1
  VCC: U1.VCC, Onderdeel1.5V
